// Logisim project FullAdder_HalfAdder.circ as structural Verilog: 2 circuits, main circuit HA
module HA (
  input  A,
  input  B,
  output S,
  output C
);

  xor xor_1 (S, A, B);
  and and_1 (C, A, B);
endmodule

module HA_Test (
  input  Cin,
  input  A,
  input  B,
  output S,
  output Cout
);

  wire ha_1_c, ha_1_s, ha_2_c;

  HA ha_1 (.A(A), .B(B), .S(ha_1_s), .C(ha_1_c));
  HA ha_2 (.A(Cin), .B(ha_1_s), .S(S), .C(ha_2_c));
  or or_1 (Cout, ha_2_c, ha_1_c);
endmodule
