// Logisim project NegativeChecker.circ as structural Verilog: 1 circuit, main circuit main
module main (
  input  a2,
  input  a1,
  input  a0,
  output out_4
);

  wire and_1_out, and_2_out, and_3_out, and_4_out, not_1_out, not_2_out, not_3_out;

  not not_1 (not_1_out, a2);
  not not_2 (not_2_out, a1);
  not not_3 (not_3_out, a0);
  and and_1 (and_1_out, a2, not_2_out, not_3_out);
  and and_2 (and_2_out, a2, not_2_out, a0);
  and and_3 (and_3_out, a2, a1, not_3_out);
  and and_4 (and_4_out, a2, a1, a0);
  or or_1 (out_4, and_1_out, and_2_out, and_3_out, and_4_out);

  // Notes on the sheet:
  //   Neg = a2a1'a0' + a2a1'a0 + a2a1a0' + a2a1a0
endmodule
