// Logisim project SignedAdditionOverflowRecognizer.circ as structural Verilog: 1 circuit, main circuit main
module main (
  input  a7,
  input  b7,
  input  c7,
  output V
);

  wire and_1_out, and_2_out, not_1_out, not_2_out, not_3_out;

  not not_1 (not_1_out, b7);
  not not_2 (not_2_out, a7);
  not not_3 (not_3_out, c7);
  and and_1 (and_1_out, not_2_out, not_1_out, c7);
  and and_2 (and_2_out, a7, b7, not_3_out);
  or or_1 (V, and_1_out, and_2_out);

  // Notes on the sheet:
  //   v = a7'b7'c7 + a7b7c7'
endmodule
