// Logisim project TwoBit_AddOne.circ as structural Verilog: 1 circuit, main circuit main
module main (
  input  a1,
  input  a0,
  output b1,
  output b0
);

  wire and_1_out, and_2_out, and_3_out, and_4_out, not_1_out, not_2_out;

  not not_1 (not_1_out, a1);
  not not_2 (not_2_out, a0);
  and and_1 (and_1_out, not_1_out, a0);
  and and_2 (and_2_out, a1, not_2_out);
  and and_3 (and_3_out, not_1_out, not_2_out);
  and and_4 (and_4_out, a1, not_2_out);
  or or_1 (b1, and_1_out, and_2_out);
  or or_2 (b0, and_3_out, and_4_out);

  // Notes on the sheet:
  //   b1 = a1'a0 + a1a0'
  //   b2 = a1'a0' + a1a0'
endmodule
