// Logisim project registers.circ as structural Verilog: 3 circuits, main circuit fourBit_serial_loader
module fourBit_serial_loader (
  input  serial_in,
  input  clk,
  output out_3,
  output out_4,
  output out_5,
  output out_6
);

  D_Flip_Flop d_ff_1 (.D(serial_in), .clk(clk), .Q(out_3));  // open: Qn, preset, reset
  D_Flip_Flop d_ff_2 (.D(out_3), .clk(clk), .Q(out_4));  // open: Qn, preset, reset
  D_Flip_Flop d_ff_3 (.D(out_4), .clk(clk), .Q(out_5));  // open: Qn, preset, reset
  D_Flip_Flop d_ff_4 (.D(out_5), .clk(clk), .Q(out_6));  // open: Qn, preset, reset
endmodule

module parallel_loader (
  input  in_1,
  input  in_2,
  input  in_3,
  input  in_4,
  input  clk,
  output out_6,
  output out_7,
  output out_8,
  output out_9
);

  D_Flip_Flop d_ff_1 (.D(in_1), .clk(clk), .Q(out_6));  // open: Qn, preset, reset
  D_Flip_Flop d_ff_2 (.D(in_2), .clk(clk), .Q(out_7));  // open: Qn, preset, reset
  D_Flip_Flop d_ff_3 (.D(in_3), .clk(clk), .Q(out_8));  // open: Qn, preset, reset
  D_Flip_Flop d_ff_4 (.D(in_4), .clk(clk), .Q(out_9));  // open: Qn, preset, reset
endmodule

module counter_4_bit (
  input  in_1,
  input  clk
);

  wire and_1_out, and_2_out, and_3_out, j_k_ff_1_q, j_k_ff_2_q, j_k_ff_3_q;

  and and_1 (and_1_out, in_1, j_k_ff_1_q);
  and and_2 (and_2_out, and_1_out, j_k_ff_2_q);
  and and_3 (and_3_out, and_2_out, j_k_ff_3_q);
  J_K_Flip_Flop j_k_ff_1 (.J(in_1), .K(in_1), .clk(clk), .Q(j_k_ff_1_q));  // open: Qn, preset, reset
  J_K_Flip_Flop j_k_ff_2 (.J(and_1_out), .K(and_1_out), .clk(clk), .Q(j_k_ff_2_q));  // open: Qn, preset, reset
  J_K_Flip_Flop j_k_ff_3 (.J(and_2_out), .K(and_2_out), .clk(clk), .Q(j_k_ff_3_q));  // open: Qn, preset, reset
  J_K_Flip_Flop j_k_ff_4 (.J(and_3_out), .K(and_3_out), .clk(clk));  // open: Q, Qn, preset, reset
endmodule
