// Logisim project reviewCircuit.circ as structural Verilog: 1 circuit, main circuit main
module main (
  input  A0,
  input  A1,
  input  A2,
  input  A3,
  output out_5
);

  wire and_1_out, and_2_out, and_3_out, not_1_out, not_2_out, not_3_out, not_4_out;

  not not_1 (not_1_out, A0);
  not not_2 (not_2_out, A1);
  not not_3 (not_3_out, A2);
  not not_4 (not_4_out, A3);
  and and_1 (and_1_out, A2, A1);
  and and_2 (and_2_out, A2, not_1_out);
  and and_3 (and_3_out, A3, A1, A0);
  or or_1 (out_5, and_1_out, and_2_out, and_3_out);
endmodule
