// Logisim project reviewCircuit2.circ as structural Verilog: 1 circuit, main circuit main
module main (
  input  x0,
  input  x1,
  input  x2,
  input  x3,
  output out_5
);

  wire and_1_out, and_2_out, not_1_out, not_2_out, not_3_out, not_4_out;

  not not_1 (not_1_out, x1);
  not not_2 (not_2_out, x0);
  not not_3 (not_3_out, x2);
  not not_4 (not_4_out, x3);
  and and_1 (and_1_out, not_3_out, x1, x0);
  and and_2 (and_2_out, x3, not_1_out, x0);
  or or_1 (out_5, and_1_out, and_2_out);

  // Notes on the sheet:
  //   F = x2'x1x0 + x3x1'x0
endmodule
